# Fritzing sketch GIT FRITZING TEST (Borisistor) (saved by Fritzing 0.9.10b)
breadboards: 1

parts:
  R1 = Resistor [tolerance=±5% power=0.25 resistance=220 package=THT]
  R2 = Resistor [tolerance=±5% power=0.25 resistance=220 package=THT]
  R3 = Resistor [tolerance=±5% power=0.25 resistance=220 package=THT]
  R4 = Resistor [tolerance=±5% power=0.25 resistance=220 package=THT]
  R5 = Resistor [tolerance=±5% power=0.25 resistance=220 package=THT]
  R6 = Resistor [tolerance=±5% power=0.25 resistance=220 package=THT]
  R7 = Resistor [tolerance=±5% power=0.25 resistance=220 package=THT]
  R8 = Resistor [tolerance=±5% power=0.25 resistance=220 package=THT]
  R9 = Resistor [tolerance=±5% power=0.25 resistance=220 package=THT]
  R10 = Resistor [tolerance=±5% power=0.25 resistance=220 package=THT]
  R11 = Resistor [tolerance=±5% power=0.25 resistance=220 package=THT]
  R12 = Resistor [tolerance=±5% power=0.25 resistance=220 package=THT]
  R13 = Resistor [tolerance=±5% power=0.25 resistance=220 package=THT]
  R14 = Resistor [tolerance=±5% power=0.25 resistance=220 package=THT]

nets:
  N1: R1.Pin_0, R3.Pin_0
  N2: R1.Pin_1, R2.Pin_1, R3.Pin_1
  N3: R4.Pin_0, R5.Pin_0
  N4: R4.Pin_1, R5.Pin_1
  N5: R6.Pin_0, R6.Pin_1, R7.Pin_0, R8.Pin_0
  N6: R9.Pin_0, R10.Pin_1
  N7: R11.Pin_0, R12.Pin_0
  N8: R12.Pin_1, R13.Pin_1
  N9: R14.Pin_0, R14.Pin_1
