# Fritzing sketch PID Tweaker Schematic (saved by Fritzing 0.9.10b)
breadboards: 1

parts:
  Arduino_Uno = Arduino Uno (Rev3)
  LCD_Screen = LCD-16X2 [package=lcd-16x2]
  R1 = Rotary Potentiometer (Small) [maximum_resistance=100kΩ knob_status=50% power=0.5W package=THT]
  R2 = Rotary Potentiometer (Large) [maximum_resistance=100kΩ knob_status=50% power=0.5W package=THT]
  R3 = Rotary Potentiometer (Large) [maximum_resistance=100kΩ knob_status=50% power=0.5W package=THT]
  R4 = Rotary Potentiometer (Large) [maximum_resistance=100kΩ knob_status=50% power=0.5W package=THT]

nets:
  A0: Arduino_Uno.A0, R2.leg2
  A1: Arduino_Uno.A1, R3.leg2
  A2: Arduino_Uno.A2, R4.leg2
  GND: Arduino_Uno.GND, LCD_Screen.K, R1.wiper, R2.wiper, R3.wiper, R4.wiper
  D2: Arduino_Uno.D2, LCD_Screen.DB4
  D3: Arduino_Uno.D3_PWM, LCD_Screen.DB5
  D4: Arduino_Uno.D4, LCD_Screen.DB6
  D5: Arduino_Uno.D5_PWM, LCD_Screen.RS
  D6: Arduino_Uno.D6_PWM, LCD_Screen.E
  D7: Arduino_Uno.D7, LCD_Screen.DB7
  5V: Arduino_Uno.5V, LCD_Screen.A, R1.leg1, R2.leg1, R3.leg1, R4.leg1
  12V: Arduino_Uno.VIN
  N1: LCD_Screen.VSS, LCD_Screen.R_W
  Contrast: LCD_Screen.VO, R1.leg2
