# Fritzing sketch Servos_Schematic (saved by Fritzing 0.9.10b)

parts:
  Left = Basic Servo
  Right = Basic Servo
  Arduino = Arduino Uno (Rev3)

nets:
  GND: Left.gnd, Right.gnd, Arduino.GND
  5V: Left.vcc, Right.vcc, Arduino.5V
  D8: Left.pulse, Arduino.D8
  D9: Right.pulse, Arduino.D9_PWM
