# Fritzing sketch Stepper Motor Drivers (without external wires) (saved by Fritzing 0.9.10b)
breadboards: 2

parts:
  Pololu_A2 = Pololu A4988 [package=SO16]
  C2 = Capacitor Polarized [package=cpol-radial-100uf-25v]
  Pololu_A1 = Pololu A4988 [package=SO16]
  C1 = Capacitor Polarized [package=cpol-radial-100uf-25v]

nets:
  N1: Pololu_A2.RESET, Pololu_A2.SLEEP
  pin 9: Pololu_A2.STEP
  pin 8: Pololu_A2.DIR
  GND: Pololu_A2.GND, C2.-, Pololu_A1.GND, C1.-
  5V: Pololu_A2.VDD, Pololu_A1.VDD
  12V: Pololu_A2.VMOT, C2.+, Pololu_A1.VMOT, C1.+
  N2: Pololu_A1.RESET, Pololu_A1.SLEEP
  pin 10: Pololu_A1.STEP
  pin 11: Pololu_A1.DIR
