# Fritzing sketch Stepper Motor Drivers (saved by Fritzing 0.9.10b)
breadboards: 2

parts:
  Pololu_A2 = Pololu A4988 [package=SO16]
  M3 = Stepper Motor - Bipolar [part_number=17HS13-0404S mpn="Nema 17"]
  C2 = Capacitor Polarized [package=cpol-radial-100uf-25v]
  Pololu_A1 = Pololu A4988 [package=SO16]
  M2 = Stepper Motor - Bipolar [part_number=17HS13-0404S mpn="Nema 17"]
  C1 = Capacitor Polarized [package=cpol-radial-100uf-25v]
  Part1 = Arduino Uno (Rev3)

nets:
  N1: Pololu_A2.RESET, Pololu_A2.SLEEP
  pin 9: Pololu_A2.STEP, Part1.D9_PWM
  pin 8: Pololu_A2.DIR, Part1.D8
  GND: Pololu_A2.GND, C2.-, Pololu_A1.GND, C1.-, Part1.GND
  5V: Pololu_A2.VDD, Pololu_A1.VDD, Part1.5V
  N2: Pololu_A2.1B, M3.D
  N3: Pololu_A2.1A, M3.B
  N4: Pololu_A2.2A, M3.C
  N5: Pololu_A2.2B, M3.A
  12V: Pololu_A2.VMOT, C2.+, Pololu_A1.VMOT, C1.+, Part1.VIN
  N6: Pololu_A1.RESET, Pololu_A1.SLEEP
  pin 10: Pololu_A1.STEP, Part1.D10_PWM/SS
  pin 11: Pololu_A1.DIR, Part1.D11_PWM/MOSI
  N7: Pololu_A1.1B, M2.D
  N8: Pololu_A1.1A, M2.B
  N9: Pololu_A1.2A, M2.C
  N10: Pololu_A1.2B, M2.A
